# Fritzing sketch DiagramaBiometrico (saved by Fritzing 0.9.3b)
breadboards: 1

parts:
  U1 = LCD-16X2 [package=lcd-16x2]
  Componente1 = Arduino Uno (Rev3)
  Componente2 = Logic Level Converter
  J1 = female pin header, 4 pins [form="♀ (female)"]
  U2 = POT [package=3362u]

nets:
  VSS: U1.VSS, U1.R_W, U1.A, Componente1.GND, U2.A
  VDD: U1.VDD, U1.K, Componente1.5V
  N1: U1.VO, U2.S
  N2: U1.RS, Componente1.D11_PWM/MOSI
  N3: U1.E, Componente1.D12/MISO
  N4: U1.DB4, Componente1.D5_PWM
  N5: U1.DB5, Componente1.D4
  N6: U1.DB6, Componente1.D3_PWM
  N7: U1.DB7, Componente1.D2
  N8: Componente1.D6_PWM, Componente2.RX2_HV
  N9: Componente1.D7, Componente2.TX2_HV
  N10: Componente1.3V3, Componente2.LV, J1.pin4
  N11: Componente2.TX2_LV, J1.pin1
  N12: Componente2.RX2_LV, J1.pin2
  N13: Componente2.GND, J1.pin3

notes:
  Negro,Blanco,Blanco,Blanco
  RX, TX, GND, 3.3Vcc
